# Fritzing sketch salak-skematik (saved by Fritzing 0.9.3b)
breadboards: 2

parts:
  A2 = JXBS-3001-NPK-RS smaller
  VCC3 = Battery  # not connected
  M6 = MAX485 Breakout [package=THT]
  M8 = DOIT Esp32 DevKit v1 (30 pins long, 11 pins width) [part_number=ESP32S-PIN30]
  M9 = MAX485 Breakout [package=THT]
  M10 = MT3608 Module
  S4 = Round Pushbutton  # not connected
  M11 = DOIT Esp32 DevKit v1 (30 pins long, 11 pins width) [part_number=ESP32S-PIN30]
  LCD2004-I2C1 = LCD2004-I2C
  VCC7 = Battery
  VCC8 = Battery  # not connected
  S5 = SPST Switch [package=r_sw_th]  # not connected
  U1 = LM2596 step down module  # not connected
  A3 = JXBS-3001-NPK-RS smaller

nets:
  N1: A2.Pin_3, M6.B
  N2: A2.Pin_4, M6.A
  N3: M6.RO, M8.D19
  N4: M6.RE, M8.D21
  N5: M6.DE, M8.D22
  N6: M6.DI, M8.D23
  N7: M9.RO, M11.RX0
  N8: M9.RE, M9.DE, M11.D2
  N9: M9.DI, M11.TX0
  GND: M9.GND, M11.GND, LCD2004-I2C1.GND
  N10: M9.A, A3.Pin_4
  N11: M9.B, A3.Pin_3
  VCC: M9.VCC, M11.VIN, LCD2004-I2C1.VCC
  N12: M10.pin1, VCC7.-
  N13: M10.pin2, VCC7.+
  N14: M10.pin3, A3.Pin_1
  N15: M10.pin4, A3.Pin_2
  N16: M11.D21, LCD2004-I2C1.SDA
  N17: M11.D22, LCD2004-I2C1.SCL

custom parts:
  JXBS-3001-NPK-RS smaller: The NPK sensor is designed for detecting the content of nitrogen, phosphorus and potassium in soil, determining the fertility of the soil and facilitating the evaluation of the soil condition by the customer system. This version has breadboard reduced in size to more closely match the 485 adapter and CPU board.
  Battery: Your standard 2x 18650 battery pack (7,4 Volts)
  MAX485 Breakout: MAX485 RS485 breakout board
  DOIT Esp32 DevKit v1 (30 pins long, 11 pins width): The DOIT Esp32 DevKit v1 is one of the development board created by DOIT to evaluate the ESP-WROOM-32 module. It is based on the ESP32 microcontroller that boasts Wifi, Bluetooth, Ethernet and Low Power support all in a single chip. (vanepp) made breadboard work, adjusted pin numbering and labels and reduced size of schematic and cleaned up pcb. This chip is 30pins long (2 x15) and 11 pins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
  MT3608 Module: MT3608 Boost Converter Module Links: Aerosemi MT3608 2A Step Up Converter datasheet
  LCD2004-I2C: A standard character display with 4x20 characters. Comes in many colors with LCM2004 IIC attached.
  LM2596 step down module: LM2596 DC-DC step down power supply module 3 A.
